// Logisim project nor_task_1.circ as structural Verilog: 1 circuit, main circuit main
module main (
  input  a,
  input  b,
  input  c,
  input  d,
  input  e,
  output y
);

  wire nor_1_out, nor_2_out, nor_3_out, nor_4_out, nor_5_out, nor_6_p5, nor_7_p5, nor_8_p5, nor_9_p5,
       nor_10_p5, nor_11_p5, nor_12_p5, nor_13_p5, nor_14_p5, nor_15_p5, nor_16_p5, nor_17_p5, nor_18_p5,
       nor_19_p5, nor_20_p5, undriven, undriven_2, undriven_3, undriven_4, undriven_5;

  not nor_1 (nor_1_out, undriven);  // NOR_Gate
  not nor_2 (nor_2_out, undriven_2);  // NOR_Gate
  not nor_3 (nor_3_out, undriven_3);  // NOR_Gate
  not nor_4 (nor_4_out, undriven_4);  // NOR_Gate
  not nor_5 (nor_5_out, undriven_5);  // NOR_Gate
  // NOR_Gate nor_6: pin names not known; wires that end beside it: a, b, d, nor_5_out, nor_6_p5
  // NOR_Gate nor_7: pin names not known; wires that end beside it: a, c, nor_4_out, e, nor_7_p5
  // NOR_Gate nor_8: pin names not known; wires that end beside it: a, b, nor_3_out, d, nor_8_p5
  // NOR_Gate nor_9: pin names not known; wires that end beside it: a, b, nor_3_out, nor_5_out, nor_9_p5
  // NOR_Gate nor_10: pin names not known; wires that end beside it: a, nor_3_out, d, nor_5_out, nor_10_p5
  // NOR_Gate nor_11: pin names not known; wires that end beside it: a, nor_2_out, c, e, nor_11_p5
  // NOR_Gate nor_12: pin names not known; wires that end beside it: a, nor_2_out, c, nor_4_out, nor_12_p5
  // NOR_Gate nor_13: pin names not known; wires that end beside it: a, nor_2_out, nor_4_out, e, nor_13_p5
  // NOR_Gate nor_14: pin names not known; wires that end beside it: nor_2_out, c, nor_4_out, e, nor_14_p5
  // NOR_Gate nor_15: pin names not known; wires that end beside it: nor_1_out, b, c, d, nor_15_p5
  // NOR_Gate nor_16: pin names not known; wires that end beside it: nor_1_out, c, d, nor_5_out, nor_16_p5
  // NOR_Gate nor_17: pin names not known; wires that end beside it: nor_1_out, b, nor_4_out, nor_5_out, nor_17_p5
  // NOR_Gate nor_18: pin names not known; wires that end beside it: nor_1_out, b, nor_3_out, e, nor_18_p5
  // NOR_Gate nor_19: pin names not known; wires that end beside it: nor_1_out, nor_2_out, nor_3_out, d, nor_19_p5
  // NOR_Gate nor_20: pin names not known; wires that end beside it: nor_1_out, nor_2_out, nor_3_out, nor_5_out, nor_20_p5
  // NOR_Gate nor_21: pin names not known; wires that end beside it: nor_6_p5, nor_7_p5, nor_8_p5, nor_9_p5, nor_10_p5, nor_11_p5, nor_12_p5, nor_13_p5, nor_14_p5, nor_15_p5, nor_16_p5, nor_17_p5, nor_18_p5, nor_19_p5, nor_20_p5, y
endmodule
