// Logisim project L08_Example.circ as structural Verilog: 3 circuits, main circuit main
module main (
  input  [31:0] Integer_variable,
  input  [63:0] in_2,
  input  [31:0] in_3,
  input  Sign,
  input  in_5,
  input  [7:0] Exponent,
  input  [22:0] Mantisa
);

  wire f32_1_s;
  wire [7:0] f32_1_p;
  wire [31:0] F32_TO_Q31_q31_mem, multiplexer_1_out;
  wire [63:0] f32_1_q, F32_TO_Q31_q31_val;

  LED led_1 (.in(f32_1_s));
  LED led_2 (.in(f32_1_s));
  Q31 F32_TO_Q31 (.F64(in_2), .Q31_Val(F32_TO_Q31_q31_val), .Q31_Mem(F32_TO_Q31_q31_mem));
  Multiplexer #(.width(32)) multiplexer_1 (
    .in0(in_3), .in1({Sign, Exponent, Mantisa}), .out(multiplexer_1_out), .sel(in_5));
  F32 f32_1 (.in_1(multiplexer_1_out), .q(f32_1_q), .p(f32_1_p), .s(f32_1_s));
  // Probe on f32_1_p
  // Probe on Integer_variable
  // Probe on Integer_variable
  // Probe on Integer_variable
  // Probe on F32_TO_Q31_q31_val
  // Probe on F32_TO_Q31_q31_mem
  // Probe on F32_TO_Q31_q31_mem
  // Probe on F32_TO_Q31_q31_mem
  // Probe on multiplexer_1_out
  // Probe on multiplexer_1_out
  // Probe on multiplexer_1_out
  // Probe on Integer_variable
  // Probe on multiplexer_1_out
  // Probe on f32_1_q

  // Notes on the sheet:
  //   Fixed-point variable
  //   Floating-point variable
  //   +
  //   =
  //   -
  //   2
  //   x
endmodule

module Q31 (
  input  [63:0] F64,
  output [63:0] Q31_Val,
  output [31:0] Q31_Mem
);

  wire [63:0] fpmultiplier_1_out, inttofp_1_p2, inttofp_2_p2;

  // IntToFP #(.fpwidth(64), .width(64)) inttofp_1: pin names not known; wires that end beside it: 64'h80000000, inttofp_1_p2
  FPDivider #(.fpwidth(64)) fpdivider_1 (.a(inttofp_2_p2), .b(inttofp_1_p2), .out(Q31_Val));
  FPMultiplier #(.fpwidth(64)) fpmultiplier_1 (.a(F64), .b(inttofp_1_p2), .out(fpmultiplier_1_out));
  // FPToInt #(.fpwidth(64), .mode("truncate"), .width(32)) fptoint_1: pin names not known; wires that end beside it: fpmultiplier_1_out, Q31_Mem
  // IntToFP #(.fpwidth(64), .width(32)) inttofp_2: pin names not known; wires that end beside it: Q31_Mem, inttofp_2_p2
endmodule

module F32 (
  input  [31:0] in_1,
  output [63:0] q,
  output [7:0] p,
  output s
);

  wire [63:0] fpdivider_1_out, inttofp_1_p2, inttofp_2_p2;

  // IntToFP #(.fpwidth(64), .mode("unsigned"), .width(23)) inttofp_1: pin names not known; wires that end beside it: in_1[22:0], inttofp_1_p2
  // IntToFP #(.fpwidth(64), .mode("unsigned"), .width(24)) inttofp_2: pin names not known; wires that end beside it: 24'h800000, inttofp_2_p2
  // Probe on fpdivider_1_out
  FPDivider #(.fpwidth(64)) fpdivider_1 (.a(inttofp_1_p2), .b(inttofp_2_p2), .out(fpdivider_1_out));
  FPAdder #(.fpwidth(64)) fpadder_1 (.a(fpdivider_1_out), .b(64'h3ff0000000000000), .out(q));
  Subtractor subtractor_1 (.a(in_1[30:23]), .b(8'h7f), .out(p));  // open: bin, bout

  assign s = in_1[31];

  // Notes on the sheet:
  //   = 2^24 = 1 << 24
  //   = 1.0 
  //   E - 127
  //   M / (2^24)  + 1
endmodule
